// Logisim project project1example.circ as structural Verilog: 2 circuits, main circuit main
module main (
  input  in_1,
  input  in_2,
  output out_3,
  output out_4,
  output out_5
);

  wire not_1_out, not_2_out;

  not not_1 (not_1_out, in_1);
  not not_2 (not_2_out, in_2);
  xnor xnor_1 (out_3, in_1, in_2);
  and and_1 (out_4, not_1_out, in_2);
  and and_2 (out_5, in_1, not_2_out);
endmodule

module onebit_compactor (
  input  in_1,
  input  in_2,
  output out_3,
  output out_4,
  output out_5
);

  wire not_1_out, not_2_out;

  not not_1 (not_1_out, in_1);
  not not_2 (not_2_out, in_2);
  xnor xnor_1 (out_3, in_1, in_2);
  and and_1 (out_4, not_1_out, in_2);
  and and_2 (out_5, in_1, not_2_out);
endmodule
